# Fritzing sketch 1. Traffic lights (saved by Fritzing 0.9.3b)
breadboards: 1

parts:
  LED4 = LED - 3mm [color="Red (633nm)" package="3 mm [THT]"]
  LED1 = smd LED [color="Red (633nm)" package="0603 [SMD]"]
  LED2 = smd LED [color="Yellow (592nm)" package="0603 [SMD]"]
  LED3 = smd LED [color="Green (555nm)" package="0603 [SMD]"]
  R1 = Resistor [tolerance=±5% resistance=220 package=THT]
  R2 = Resistor [tolerance=±5% resistance=220 package="0402 [SMD]"]
  R3 = Resistor [tolerance=±5% resistance=220 package="0402 [SMD]"]
  R4 = Resistor [tolerance=±5% resistance=220 package=THT]
  R5 = Resistor [tolerance=±5% resistance=220 package=THT]
  S1 = Pushbutton [package="[SMD]"]
  LED5 = LED - 3mm [color="Green (555nm)" package="3 mm [THT]"]
  Part1 = Arduino Uno (Rev3) - ICSP
  R6 = Resistor [tolerance=±5% resistance=10 package=THT]

nets:
  N1: LED4.cathode, R2.Pin_1
  N2: LED4.anode, Part1.D3_PWM
  N3: LED1.cathode, R5.Pin_1
  N4: LED1.anode, Part1.D13/SCK
  N5: LED2.cathode, R4.Pin_1
  N6: LED2.anode, Part1.D12/MISO
  N7: LED3.cathode, R1.Pin_1
  N8: LED3.anode, Part1.D11_PWM/MOSI
  N9: R1.Pin_0, R2.Pin_0, R3.Pin_0, R4.Pin_0, R5.Pin_0, Part1.GND, R6.Pin_0
  N10: R3.Pin_1, LED5.cathode
  N11: S1.Pin_1, S1.Pin_2, Part1.5V
  N12: S1.Pin_3, S1.Pin_4, Part1.D7, R6.Pin_1
  N13: LED5.anode, Part1.D2
